# Fritzing sketch FirmataMaster (NodeMCU) with Arduino Uno (saved by Fritzing 0.9.3b)
breadboards: 1

parts:
  BB1 = 4-Line Bi-Directional Level Shifter
  Arduino_Uno = Arduino Uno (Rev3) - ICSP
  Debug_port = FTDI Basic Programmer
  U1 = NodeMCU V1.0

nets:
  N1: BB1.LV, U1.D5
  N2: BB1.A1, U1.D7
  N3: BB1.A2, U1.D8
  GND: BB1.GND, Arduino_Uno.GND, Debug_port.GND, U1.GND
  5V: BB1.HV, U1.Vin
  N4: BB1.B1, Arduino_Uno.D1/TX
  N5: BB1.B2, Arduino_Uno.D0/RX
  N6: Debug_port.RXI, U1.D6

notes:
  Debug port. Optional.
  Level converter

custom parts:
  4-Line Bi-Directional Level Shifter: 4-Channel Bi-Directional Level Shifter
  NodeMCU V1.0: ESP8266 based NodeMCU
